# Fritzing sketch EsquemaDRAGON (saved by Fritzing 1.0.2b)

parts:
  M1 = DC Motor [voltage_(max)=6V voltage_(min)=3V]  # not connected
  M2 = DC Motor [voltage_(max)=6V voltage_(min)=3V]  # not connected
  A1 = drv-1012
  A2 = drv-1012
  Componente1 = Arduino Mega 2560 (Rev3)  # not connected
  HC-SR04_Sensor_1 = HC-SR04 Ultrasonic Distance Sensor  # not connected
  HC-SR04_Sensor_2 = HC-SR04 Ultrasonic Distance Sensor  # not connected
  HC-SR04_Sensor_3 = HC-SR04 Ultrasonic Distance Sensor  # not connected
  HC-SR04_Sensor_4 = HC-SR04 Ultrasonic Distance Sensor  # not connected
  J1 = Basic Servo  # not connected
  J2 = Basic Servo  # not connected
  J3 = Basic Servo  # not connected
  J4 = Basic Servo  # not connected
  J5 = Basic Servo  # not connected
  J6 = Basic Servo  # not connected
  Componente2 = Adafruit BNO055 STEMMA QT [part_number="Adafruit #4646"]  # not connected
  Componente3 = TE466 [part_number=TE466]  # not connected
  Componente4 = Adafruit PCA9685 PWM/Servo Breakout [part_number=815]  # not connected
  M3 = RioRand LM2596  # not connected
  M4 = RioRand LM2596  # not connected
  M5 = RioRand LM2596  # not connected
  M6 = DC Motor [voltage_(max)=6V voltage_(min)=3V]  # not connected
  M7 = DC Motor [voltage_(max)=6V voltage_(min)=3V]  # not connected

nets:
  N1: A1.Pin_11, A2.Pin_11
  N2: A1.Pin_12, A2.Pin_12

custom parts:
  drv-1012: .The BTS7960 is a fully integrated high current H bridge module for motor drive applications.
  Adafruit BNO055 STEMMA QT: If you've ever ordered and wire up a 9-DOF sensor, chances are you've also realized the challenge of turning the sensor data from an accelerometer, gyroscope, and magnetometer into actual "3D space orientation"! Orientation is a hard problem to solve. The sensor fusion algorithms (the secret sauce that blends accelerometer, magnetometer, and gyroscope data into stable three-axis orientation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
  TE466: Description: This is essentially a ramped up version of our Ardumoto motor driver shield. For this monster shield we've replaced the L298 H-bridge with a pair of VNH2SP30 full-bridge motor drivers. We've also beefed up the support circuitry so this board is capable of driving a pair of high-current motors! The VIN and motor out are pitched for our 5mm screw terminals (not included), making it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
  Adafruit PCA9685 PWM/Servo Breakout: Using only two pins, control 16 free-running PWM outputs! I2C-controlled PWM driver with a built in clock. Unlike the TLC5940 family, you do not need to continuously send it signal tying up your microcontroller, its completely free running! 5V compliant, which means you can control it from a 3.3V microcontroller and still safely drive up to 6V outputs (this is good for when you want to control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
